// Logisim project 74194ShiftRegister.circ as structural Verilog: 1 circuit, main circuit main
module main (
  input  in_1,
  input  B,
  input  C,
  input  D,
  input  SERIAL_INPUT,
  input  SERIAL_INPUT_2,
  input  S0,
  input  S1,
  input  CLEAR,
  output out_10,
  output out_11,
  output out_12,
  output out_13
);

  wire clock_1_out, d_ff_1_qn, d_ff_2_qn, d_ff_3_qn, d_ff_4_qn, nand_1_out, nand_2_out, nand_3_out,
       nand_4_out, not_1_out, not_2_out, not_3_out, not_4_out, not_6_out, not_8_out, not_10_out, not_11_out,
       or_1_out, or_2_out, or_3_out, or_4_out, or_5_out, or_6_out, or_7_out, or_8_out, or_9_out, or_10_out,
       or_11_out, or_12_out, or_13_out, or_14_out, or_15_out, or_16_out;

  Clock clock_1 (.out(clock_1_out));
  not not_1 (not_1_out, SERIAL_INPUT);
  not not_2 (not_2_out, S0);
  not not_3 (not_3_out, S1);
  or or_1 (or_1_out, not_1_out, not_2_out, S1);
  not not_4 (not_4_out, in_1);
  or or_2 (or_2_out, not_3_out, S0, d_ff_2_qn);
  or or_3 (or_3_out, S1, S0, not_4_out);
  nand nand_1 (nand_1_out, or_1_out, or_3_out, or_2_out, or_4_out);
  or or_4 (or_4_out, not_3_out, not_2_out, d_ff_1_qn);
  D_Flip_Flop d_ff_1 (.clk(clock_1_out), .D(nand_1_out), .Qn(d_ff_1_qn), .reset(CLEAR));  // open: Q, preset, en
  not not_5 (out_10, d_ff_1_qn);
  not not_6 (not_6_out, B);
  or or_5 (or_5_out, d_ff_1_qn, not_2_out, S1);
  or or_6 (or_6_out, S1, S0, not_6_out);
  nand nand_2 (nand_2_out, or_5_out, or_6_out, or_8_out, or_7_out);
  or or_7 (or_7_out, not_3_out, not_2_out, d_ff_2_qn);
  or or_8 (or_8_out, not_3_out, S0, d_ff_3_qn);
  D_Flip_Flop d_ff_2 (.clk(clock_1_out), .D(nand_2_out), .Qn(d_ff_2_qn), .reset(CLEAR));  // open: Q, preset, en
  not not_7 (out_11, d_ff_2_qn);
  or or_9 (or_9_out, d_ff_2_qn, not_2_out, S1);
  or or_10 (or_10_out, S1, S0, not_8_out);
  not not_8 (not_8_out, C);
  or or_11 (or_11_out, not_3_out, not_2_out, d_ff_3_qn);
  or or_12 (or_12_out, not_3_out, S0, d_ff_4_qn);
  nand nand_3 (nand_3_out, or_9_out, or_10_out, or_12_out, or_11_out);
  D_Flip_Flop d_ff_3 (.clk(clock_1_out), .D(nand_3_out), .Qn(d_ff_3_qn), .reset(CLEAR));  // open: Q, preset, en
  or or_13 (or_13_out, d_ff_3_qn, not_2_out, S1);
  not not_9 (out_12, d_ff_3_qn);
  not not_10 (not_10_out, D);
  or or_14 (or_14_out, S1, S0, not_10_out);
  or or_15 (or_15_out, not_3_out, S0, not_11_out);
  nand nand_4 (nand_4_out, or_13_out, or_14_out, or_15_out, or_16_out);
  not not_11 (not_11_out, SERIAL_INPUT_2);
  or or_16 (or_16_out, not_3_out, not_2_out, d_ff_4_qn);
  D_Flip_Flop d_ff_4 (.clk(clock_1_out), .D(nand_4_out), .Qn(d_ff_4_qn), .reset(CLEAR));  // open: Q, preset, en
  not not_12 (out_13, d_ff_4_qn);

  // Notes on the sheet:
  //   CLOCK
  //   SHIFT RIGHT
  //   A
  //   QA
  //   QB
  //   QC
  //   SHIFT LEFT
  //   QD
endmodule
