// Logisim project 74194ShiftRegisterPodPktB.circ as structural Verilog: 1 circuit, main circuit main
module main (
  input  CLEAR_S1,
  output out_2,
  output out_3,
  output out_4,
  output out_5
);

  wire and_1_out, and_2_out, and_3_out, and_4_out, and_5_out, and_6_out, and_7_out, and_8_out, and_9_out,
       and_10_out, and_11_out, and_12_out, and_13_out, clock_1_out, nand_1_out, nor_1_out, nor_2_out,
       nor_3_out, nor_4_out, nor_5_out, nor_6_out, not_1_out, not_2_out, not_3_out, not_4_out, not_5_out,
       not_6_out, not_7_out, not_8_out, not_9_out, not_10_out, not_11_out;

  Clock clock_1 (.out(clock_1_out));
  not not_1 (not_1_out, 1'b0);
  not not_2 (not_2_out, CLEAR_S1);
  not not_3 (not_3_out, CLEAR_S1);
  nor nor_1 (nor_1_out, not_1_out, not_2_out);
  buf and_1 (and_1_out, not_2_out);  // AND_Gate
  and and_2 (and_2_out, not_1_out, not_2_out);
  and and_3 (and_3_out, not_1_out, out_3);
  buf and_4 (and_4_out, nor_1_out);  // AND_Gate
  nor nor_2 (nor_2_out, and_1_out, and_4_out, and_3_out);
  nor nor_3 (nor_3_out, and_2_out, clock_1_out);
  not not_4 (not_4_out, nor_2_out);
  and and_5 (and_5_out, out_2, not_2_out);
  not not_5 (not_5_out, nor_3_out);
  S_R_Flip_Flop s_r_ff_1 (
    .S(not_4_out), .clk(not_5_out), .R(nor_2_out), .Q(out_2), .reset(not_3_out));  // open: Qn, preset, en
  and and_6 (and_6_out, not_1_out, out_4);
  buf and_7 (and_7_out, nor_1_out);  // AND_Gate
  nor nor_4 (nor_4_out, and_5_out, and_7_out, and_6_out);
  not not_6 (not_6_out, nor_4_out);
  and and_8 (and_8_out, out_3, not_2_out);
  not not_7 (not_7_out, nor_3_out);
  S_R_Flip_Flop s_r_ff_2 (
    .S(not_6_out), .clk(not_7_out), .R(nor_4_out), .Q(out_3), .reset(not_3_out));  // open: Qn, preset, en
  and and_9 (and_9_out, not_1_out, out_5);
  buf and_10 (and_10_out, nor_1_out);  // AND_Gate
  nor nor_5 (nor_5_out, and_8_out, and_10_out, and_9_out);
  not not_8 (not_8_out, nor_5_out);
  and and_11 (and_11_out, out_4, not_2_out);
  not not_9 (not_9_out, nor_3_out);
  S_R_Flip_Flop s_r_ff_3 (
    .S(not_8_out), .clk(not_9_out), .R(nor_5_out), .Q(out_4), .reset(not_3_out));  // open: Qn, preset, en
  buf and_12 (and_12_out, nor_1_out);  // AND_Gate
  and and_13 (and_13_out, not_1_out, nand_1_out);
  nor nor_6 (nor_6_out, and_11_out, and_12_out, and_13_out);
  not not_10 (not_10_out, nor_6_out);
  not not_11 (not_11_out, nor_3_out);
  S_R_Flip_Flop s_r_ff_4 (
    .S(not_10_out), .clk(not_11_out), .R(nor_6_out), .Q(out_5), .reset(not_3_out));  // open: Qn, preset, en
  nand nand_1 (nand_1_out, out_3, out_4, out_5);

  // Notes on the sheet:
  //   CLOCK
  //   QA
  //   QB
  //   QC
  //   QD
endmodule
