// Logisim project UkladZHazardemIBez.circ as structural Verilog: 1 circuit, main circuit main
module main (
  input  A,
  input  B,
  input  C,
  input  D,
  input  A_2,
  input  B_2,
  input  C_2,
  input  D_2
);

  wire d_ff_1_q, d_ff_1_qn, d_ff_2_q, d_ff_2_qn, nand_1_out, nand_2_out, nand_3_out, nand_4_out, nand_5_out,
       nand_6_out, nand_7_out, nand_8_out, nand_9_out, nand_10_out, not_1_out, not_2_out, not_3_out,
       not_4_out, not_5_out, not_6_out, not_7_out, not_8_out;

  not not_1 (not_1_out, C);
  not not_2 (not_2_out, A);
  not not_3 (not_3_out, D);
  not not_4 (not_4_out, C_2);
  not not_5 (not_5_out, A_2);
  not not_6 (not_6_out, D_2);
  not not_7 (not_7_out, A_2);
  not not_8 (not_8_out, A_2);
  nand nand_1 (nand_1_out, B, not_1_out, D);
  nand nand_2 (nand_2_out, not_2_out, C, D);
  nand nand_3 (nand_3_out, B, C, not_3_out);
  nand nand_4 (nand_4_out, B_2, not_4_out, D_2);
  nand nand_5 (nand_5_out, not_5_out, C_2, D_2);
  nand nand_6 (nand_6_out, B_2, C_2, not_6_out);
  nand nand_7 (nand_7_out, not_7_out, B_2, C_2);
  nand nand_8 (nand_8_out, not_8_out, B_2, D_2);
  nand nand_9 (nand_9_out, nand_1_out, nand_2_out, nand_3_out);
  nand nand_10 (nand_10_out, nand_4_out, nand_5_out, nand_6_out, nand_7_out, nand_8_out);
  LED led_1 (.in(nand_10_out));
  D_Flip_Flop d_ff_1 (.clk(nand_9_out), .D(d_ff_1_qn), .Q(d_ff_1_q), .Qn(d_ff_1_qn));  // open: preset, en, reset
  LED led_2 (.in(nand_9_out));
  D_Flip_Flop d_ff_2 (.clk(nand_10_out), .D(d_ff_2_qn), .Q(d_ff_2_q), .Qn(d_ff_2_qn));  // open: preset, en, reset
  LED led_3 (.in(d_ff_1_q));
  LED led_4 (.in(d_ff_2_q));

  // Notes on the sheet:
  //   Układ z hazardem
  //   Układ bez hazardu
  //   LED 1
  //   LED 1
  //   LED 2
  //   LED 2
endmodule
