// Logisim project Zadanie2PodPktA.circ as structural Verilog: 1 circuit, main circuit main
module main (
  input  A,
  input  B,
  input  C,
  input  D,
  input  A_2,
  input  B_2,
  input  C_2,
  input  D_2,
  input  A_3,
  input  B_3,
  input  C_3,
  input  D_3,
  input  A_4,
  input  B_4,
  input  C_4,
  input  A_5,
  input  B_5,
  input  C_5,
  input  G,
  input  D0,
  input  D1,
  input  D2,
  input  D3,
  input  D4,
  input  D5,
  input  D6,
  input  D7,
  input  A_6,
  input  B_6,
  input  C_6,
  input  G_D,
  input  G_2,
  input  A_7,
  input  A_8,
  input  B_7,
  input  B_8,
  input  C_7,
  input  C_8,
  output out_39
);

  wire and_1_out, and_2_out, and_3_out, and_4_out, and_5_out, and_6_out, and_7_out, and_8_out, and_9_out,
       and_10_out, and_11_out, and_12_out, and_13_out, and_14_out, and_15_out, and_16_out, and_17_out,
       and_18_out, and_19_out, and_20_out, and_21_out, and_22_out, and_23_out, and_24_out, and_25_out,
       and_26_out, and_27_out, and_28_out, and_29_out, nand_1_out, nand_2_out, nand_3_out, nand_4_out,
       nand_5_out, nand_6_out, nand_7_out, nand_8_out, nand_9_out, nand_10_out, nand_11_out, nand_12_out,
       nand_13_out, nand_14_out, nand_15_out, nand_16_out, nor_1_out, nor_2_out, nor_3_out, not_1_out,
       not_2_out, not_3_out, not_4_out, not_5_out, not_6_out, not_7_out, not_8_out, not_9_out, not_10_out,
       not_11_out, not_12_out, not_13_out, not_14_out, not_15_out, not_16_out, not_17_out, not_18_out,
       not_19_out, not_20_out, not_21_out, not_22_out, not_23_out, not_24_out, not_25_out, not_26_out,
       not_27_out, not_28_out, not_29_out, not_30_out, not_31_out, not_32_out, not_33_out, not_34_out,
       not_35_out, not_36_out, not_37_out, not_38_out, not_39_out, not_40_out, not_41_out, not_42_out,
       not_43_out, not_44_out, not_45_out, not_46_out, not_47_out, not_48_out, not_49_out, not_50_out,
       not_51_out, not_52_out, not_53_out, or_1_out, or_2_out;

  not not_1 (not_1_out, A_7);
  not not_2 (not_2_out, B_7);
  not not_3 (not_3_out, C_7);
  not not_4 (not_4_out, G_D);
  not not_5 (not_5_out, not_1_out);
  not not_6 (not_6_out, not_2_out);
  not not_7 (not_7_out, not_3_out);
  not not_8 (not_8_out, C_2);
  not not_9 (not_9_out, D_2);
  not not_10 (not_10_out, A_2);
  not not_11 (not_11_out, B_2);
  not not_12 (not_12_out, D_2);
  not not_13 (not_13_out, A_4);
  not not_14 (not_14_out, C_4);
  not not_15 (not_15_out, B_4);
  not not_16 (not_16_out, not_17_out);
  not not_17 (not_17_out, A_6);
  not not_18 (not_18_out, B_6);
  not not_19 (not_19_out, not_18_out);
  not not_20 (not_20_out, C_6);
  not not_21 (not_21_out, not_20_out);
  and and_1 (and_1_out, not_8_out, not_9_out);
  and and_2 (and_2_out, not_10_out, not_11_out, C_2, not_12_out);
  and and_3 (and_3_out, not_13_out, not_14_out);
  and and_4 (and_4_out, B_4, C_4);
  and and_5 (and_5_out, A_4, not_15_out);
  not not_22 (not_22_out, G);
  not not_23 (not_23_out, A_7);
  not not_24 (not_24_out, B_7);
  nand nand_1 (nand_1_out, not_23_out, not_24_out, C_7, not_25_out);
  not not_25 (not_25_out, G_D);
  not not_26 (not_26_out, C_7);
  nand nand_2 (nand_2_out, not_26_out, not_27_out);
  not not_27 (not_27_out, G_D);
  or or_1 (or_1_out, and_1_out, and_2_out);
  or or_2 (or_2_out, and_3_out, and_4_out, and_5_out);
  and and_6 (and_6_out, 1'b1, not_1_out, not_2_out, not_3_out, not_4_out);
  and and_7 (and_7_out, 1'b1, not_5_out, not_2_out, not_3_out, not_4_out);
  and and_8 (and_8_out, 1'b1, not_1_out, not_6_out, not_3_out, not_4_out);
  and and_9 (and_9_out, 1'b1, not_5_out, not_6_out, not_3_out, not_4_out);
  and and_10 (and_10_out, 1'b1, not_7_out, not_1_out, not_2_out, not_4_out);
  and and_11 (and_11_out, 1'b0, not_5_out, not_2_out, not_7_out, not_4_out);
  and and_12 (and_12_out, 1'b0, not_1_out, not_6_out, not_7_out, not_4_out);
  and and_13 (and_13_out, 1'b0, not_5_out, not_6_out, not_7_out, not_4_out);
  LED led_1 (.in(or_1_out));
  LED led_2 (.in(or_2_out));
  and and_14 (and_14_out, D0, not_17_out, not_18_out, not_20_out, not_22_out);
  and and_15 (and_15_out, D1, not_16_out, not_18_out, not_20_out, not_22_out);
  and and_16 (and_16_out, D2, not_17_out, not_19_out, not_20_out, not_22_out);
  and and_17 (and_17_out, D3, not_16_out, not_19_out, not_20_out, not_22_out);
  and and_18 (and_18_out, D4, not_21_out, not_17_out, not_18_out, not_22_out);
  and and_19 (and_19_out, D5, not_16_out, not_18_out, not_21_out, not_22_out);
  and and_20 (and_20_out, D6, not_17_out, not_19_out, not_21_out, not_22_out);
  and and_21 (and_21_out, D7, not_16_out, not_19_out, not_21_out, not_22_out);
  nand nand_3 (nand_3_out, nand_1_out, nand_2_out);
  nor nor_1 (nor_1_out, and_6_out, and_7_out, and_8_out, and_9_out, and_10_out, and_11_out, and_12_out, and_13_out);
  nor nor_2 (nor_2_out, and_14_out, and_15_out, and_16_out, and_17_out, and_18_out, and_19_out, and_20_out, and_21_out);
  LED led_3 (.in(not_28_out));
  not not_28 (not_28_out, nor_1_out);
  LED led_4 (.in(nand_3_out));
  not not_29 (not_29_out, nor_2_out);
  LED led_5 (.in(not_29_out));
  LED led_6 (.in(nor_2_out));
  not not_30 (not_30_out, A_3);
  not not_31 (not_31_out, B_3);
  nand nand_4 (nand_4_out, not_30_out, not_31_out, C_3, not_32_out);
  not not_32 (not_32_out, D_3);
  not not_33 (not_33_out, C_3);
  nand nand_5 (nand_5_out, not_33_out, not_34_out);
  not not_34 (not_34_out, D_3);
  not not_35 (not_35_out, A_5);
  nand nand_6 (nand_6_out, not_35_out, not_36_out);
  not not_36 (not_36_out, C_5);
  nand nand_7 (nand_7_out, B_5, C_5);
  nand nand_8 (nand_8_out, A_5, not_37_out);
  not not_37 (not_37_out, B_5);
  not not_38 (not_38_out, A_8);
  not not_39 (not_39_out, B_8);
  not not_40 (not_40_out, C_8);
  not not_41 (not_41_out, not_38_out);
  not not_42 (not_42_out, not_39_out);
  not not_43 (not_43_out, not_40_out);
  LED led_7 (.in(nand_9_out));
  nand nand_9 (nand_9_out, nand_4_out, nand_5_out);
  nand nand_10 (nand_10_out, nand_6_out, nand_7_out, nand_8_out);
  LED led_8 (.in(nand_10_out));
  not not_44 (not_44_out, G_2);
  not not_45 (not_45_out, A_8);
  not not_46 (not_46_out, C_8);
  not not_47 (not_47_out, B_8);
  and and_22 (and_22_out, 1'b1, not_38_out, not_39_out, not_40_out, not_44_out);
  and and_23 (and_23_out, 1'b1, not_41_out, not_39_out, not_40_out, not_44_out);
  and and_24 (and_24_out, 1'b1, not_38_out, not_42_out, not_40_out, not_44_out);
  and and_25 (and_25_out, 1'b0, not_41_out, not_42_out, not_40_out, not_44_out);
  and and_26 (and_26_out, 1'b0, not_43_out, not_38_out, not_39_out, not_44_out);
  and and_27 (and_27_out, 1'b1, not_41_out, not_39_out, not_43_out, not_44_out);
  and and_28 (and_28_out, 1'b1, not_38_out, not_42_out, not_43_out, not_44_out);
  and and_29 (and_29_out, 1'b1, not_41_out, not_42_out, not_43_out, not_44_out);
  nand nand_11 (nand_11_out, not_45_out, not_46_out);
  nand nand_12 (nand_12_out, B_8, C_8);
  nand nand_13 (nand_13_out, A_8, not_47_out);
  nor nor_3 (nor_3_out, and_22_out, and_23_out, and_24_out, and_25_out, and_26_out, and_27_out, and_28_out, and_29_out);
  nand nand_14 (nand_14_out, nand_11_out, nand_12_out, nand_13_out);
  not not_48 (not_48_out, nor_3_out);
  not not_49 (not_49_out, A);
  not not_50 (not_50_out, B);
  nand nand_15 (nand_15_out, not_49_out, not_50_out, C, not_51_out);
  not not_51 (not_51_out, D);
  not not_52 (not_52_out, C);
  nand nand_16 (nand_16_out, not_52_out, not_53_out);
  not not_53 (not_53_out, D);
  LED led_9 (.in(not_48_out));
  LED led_10 (.in(nand_14_out));
  nand nand_17 (out_39, nand_15_out, nand_16_out);

  // Notes on the sheet:
  //   Zoptymalizowana funkcja a
  //   AND/OR VERSION
  //   Zoptymalizowana funkcja b
  //   AND/OR VERSION
  //   Układ 74151
  //   Inputs
  //   Funkcja a na układzie MUX
  //   D0
  //   D1
  //   D2
  //   D3
  //   D4
  //   D5
  //   D6
  //   D7
  //   NAND VERSION
  //   NAND VERSION
  //   Outputs
  //   Y
  //   W
  //   Funkcja b na układzie MUX
  //   D0
  //   D1
  //   D2
  //   D3
  //   D4
  //   D5
  //   D6
  //   D7
  //   Zoptymalizowana funkcja a(NAND)
endmodule
