// Logisim project zadanie 5.circ as structural Verilog: 1 circuit, main circuit main
module main (
  input  X,
  output Z1,
  output Z2,
  output Z1_2,
  output Z2_2
);

  wire and_1_out, and_2_out, clock_1_out, d_ff_1_q, d_ff_1_qn, d_ff_2_q, d_ff_2_qn, j_k_ff_1_q, j_k_ff_1_qn,
       not_1_out, or_1_out;

  Clock clock_1 (.out(clock_1_out));
  not not_1 (not_1_out, X);
  and and_1 (and_1_out, d_ff_1_q, not_1_out);
  and and_2 (and_2_out, X, d_ff_1_qn);
  J_K_Flip_Flop j_k_ff_1 (
    .J(X), .clk(clock_1_out), .K(X), .Q(j_k_ff_1_q), .Qn(j_k_ff_1_qn));  // open: preset, en, reset
  or or_1 (or_1_out, and_1_out, and_2_out);
  D_Flip_Flop d_ff_1 (.clk(clock_1_out), .D(or_1_out), .Q(d_ff_1_q), .Qn(d_ff_1_qn));  // open: preset, en, reset
  D_Flip_Flop d_ff_2 (.clk(clock_1_out), .D(d_ff_1_q), .Q(d_ff_2_q), .Qn(d_ff_2_qn));  // open: preset, en, reset
  and and_3 (Z1_2, X, j_k_ff_1_qn);
  and and_4 (Z2_2, j_k_ff_1_q, X);
  and and_5 (Z1, d_ff_1_q, d_ff_2_qn);
  and and_6 (Z2, d_ff_1_qn, d_ff_2_q);

  // Notes on the sheet:
  //   CLOCK
  //   J
  //   K
  //   Q1
  //   neg Q1
  //   D1
  //   D2
endmodule
